// Logisim project e2644409.circ as structural Verilog: 1 circuit, main circuit main
module main (
  input  O3,
  input  O2,
  input  O1,
  input  O0,
  input  A1,
  input  A0,
  input  B1,
  input  B0,
  output S,
  output C,
  output Z,
  output P,
  output E,
  output G,
  output L,
  output L9,
  output L9_2,
  output L8,
  output L7,
  output L6,
  output L5,
  output L4,
  output L3,
  output L2,
  output L1,
  output L0
);

  wire and_1_out, and_2_out, and_3_out, and_4_out, and_5_out, and_6_out, and_7_out, and_8_out, and_9_out,
       and_10_out, and_11_out, and_12_out, and_13_out, and_14_out, and_15_out, and_16_out, and_17_out,
       and_18_out, and_19_out, and_20_out, and_21_out, and_22_out, and_23_out, and_24_out, and_25_out,
       and_26_out, and_27_out, and_28_out, and_29_out, and_30_out, and_31_out, and_32_out, and_33_out,
       and_34_out, and_35_out, and_36_out, and_37_out, and_38_out, and_39_out, and_40_out, and_41_out,
       and_42_out, and_43_out, and_44_out, and_45_out, n3_to_8_decoder_74138_1_p7,
       n3_to_8_decoder_74138_1_p8, n3_to_8_decoder_74138_1_p9, n3_to_8_decoder_74138_1_p10,
       n3_to_8_decoder_74138_1_p11, n3_to_8_decoder_74138_1_p12, n3_to_8_decoder_74138_1_p13,
       n3_to_8_decoder_74138_1_p14, n3_to_8_decoder_74138_2_p4, n3_to_8_decoder_74138_2_p5,
       n3_to_8_decoder_74138_2_p6, n3_to_8_decoder_74138_3_p7, n3_to_8_decoder_74138_3_p8,
       n3_to_8_decoder_74138_3_p9, n3_to_8_decoder_74138_4_p10, n3_to_8_decoder_74138_4_p11,
       n3_to_8_decoder_74138_5_p4, n3_to_8_decoder_74138_6_p10, n3_to_8_decoder_74138_7_p7,
       n3_to_8_decoder_74138_7_p8, n3_to_8_decoder_74138_7_p9, n3_to_8_decoder_74138_7_p10,
       n3_to_8_decoder_74138_8_p7, n3_to_8_decoder_74138_9_p7, n3_to_8_decoder_74138_10_p7,
       n3_to_8_decoder_74138_10_p8, n3_to_8_decoder_74138_11_p8, n3_to_8_decoder_74138_12_p7,
       n3_to_8_decoder_74138_12_p8, n3_to_8_decoder_74138_12_p9, n3_to_8_decoder_74138_12_p10,
       n3_to_8_decoder_74138_12_p11, n3_to_8_decoder_74138_12_p12, n3_to_8_decoder_74138_12_p13,
       n3_to_8_decoder_74138_13_p3, n3_to_8_decoder_74138_13_p7, n3_to_8_decoder_74138_13_p8,
       n3_to_8_decoder_74138_13_p9, n3_to_8_decoder_74138_13_p10, n3_to_8_decoder_74138_13_p11,
       n3_to_8_decoder_74138_13_p12, n3_to_8_decoder_74138_13_p13, n3_to_8_decoder_74138_14_p7,
       n3_to_8_decoder_74138_14_p8, n3_to_8_decoder_74138_14_p9, n3_to_8_decoder_74138_14_p10,
       n3_to_8_decoder_74138_14_p11, n3_to_8_decoder_74138_14_p12, nand_1_out, nand_2_out, nor_1_out,
       nor_2_out, nor_3_out, nor_4_out, not_1_out, not_2_out, not_3_out, not_4_out, not_5_out, not_6_out,
       not_7_out, not_8_out, not_9_out, not_10_out, not_11_out, not_12_out, not_13_out, not_14_out,
       not_15_out, not_16_out, not_17_out, not_18_out, not_19_out, not_20_out, not_21_out, not_22_out,
       not_23_out, not_24_out, not_25_out, not_26_out, not_27_out, not_28_out, not_29_out, not_30_out,
       not_31_out, not_32_out, not_33_out, not_34_out, not_35_out, not_36_out, not_37_out, not_38_out,
       not_39_out, not_40_out, not_41_out, not_42_out, not_43_out, not_44_out, not_45_out, not_46_out,
       not_47_out, not_48_out, not_49_out, not_50_out, not_51_out, not_52_out, not_53_out, not_54_out,
       not_55_out, not_56_out, not_57_out, not_58_out, not_59_out, not_60_out, not_61_out, not_62_out,
       or_1_out, or_2_out, or_3_out, or_4_out, or_5_out, or_6_out, or_7_out, or_8_out, or_9_out, or_10_out,
       or_11_out, or_13_out, or_14_out, or_15_out, or_16_out, or_17_out, or_18_out, or_19_out, or_20_out,
       or_21_out, or_22_out, or_23_out, or_24_out, or_25_out, or_26_out, or_27_out, or_28_out, or_29_out,
       or_30_out, or_31_out, or_32_out, or_33_out, or_34_out, xor_1_out, xor_2_out, xor_3_out, xor_4_out,
       xor_5_out, xor_6_out, xor_7_out, xor_8_out, xor_9_out, xor_10_out, xor_11_out, xor_12_out;

  and and_1 (and_1_out, O3, not_9_out);
  // _3_to_8_decoder__74138 #(.Facing("east")) 3_to_8_decoder_74138_1: pin names not known; wires that end beside it: O2, O1, O0, 1'b1, 1'b0, 1'b0, n3_to_8_decoder_74138_1_p7, n3_to_8_decoder_74138_1_p8, n3_to_8_decoder_74138_1_p9, n3_to_8_decoder_74138_1_p10, n3_to_8_decoder_74138_1_p11, n3_to_8_decoder_74138_1_p12, n3_to_8_decoder_74138_1_p13, n3_to_8_decoder_74138_1_p14
  not not_1 (not_1_out, O3);
  not not_2 (not_2_out, n3_to_8_decoder_74138_1_p14);
  not not_3 (not_3_out, n3_to_8_decoder_74138_1_p13);
  not not_4 (not_4_out, n3_to_8_decoder_74138_1_p11);
  not not_5 (not_5_out, n3_to_8_decoder_74138_1_p12);
  not not_6 (not_6_out, n3_to_8_decoder_74138_1_p10);
  not not_7 (not_7_out, n3_to_8_decoder_74138_1_p9);
  not not_8 (not_8_out, n3_to_8_decoder_74138_1_p8);
  not not_9 (not_9_out, n3_to_8_decoder_74138_1_p7);
  and and_2 (and_2_out, not_9_out, not_1_out);
  not not_10 (not_10_out, A1);
  not not_11 (not_11_out, A0);
  not not_12 (not_12_out, B1);
  not not_13 (not_13_out, B0);
  xor xor_1 (xor_1_out, A0, B0);
  and and_3 (and_3_out, B0, A0);
  and and_4 (and_4_out, B1, not_10_out);
  and and_5 (and_5_out, not_10_out, not_11_out);
  and and_6 (and_6_out, and_5_out, B0);
  and and_7 (and_7_out, B0, not_11_out);
  xor xor_2 (xor_2_out, A0, B0);
  and and_8 (and_8_out, B0, not_14_out);
  not not_14 (not_14_out, A0);
  and and_9 (and_9_out, A0, B0);
  and and_10 (and_10_out, A1, B0);
  and and_11 (and_11_out, A0, B1);
  and and_12 (and_12_out, A1, B1);
  // _3_to_8_decoder__74138 #(.Facing("east")) 3_to_8_decoder_74138_2: pin names not known; wires that end beside it: A1, A0, B1, n3_to_8_decoder_74138_2_p4, n3_to_8_decoder_74138_2_p5, n3_to_8_decoder_74138_2_p6
  // _3_to_8_decoder__74138 #(.Facing("east")) 3_to_8_decoder_74138_3: pin names not known; wires that end beside it: A0, B1, B0, not_5_out, 1'b0, 1'b0, n3_to_8_decoder_74138_3_p7, n3_to_8_decoder_74138_3_p8, n3_to_8_decoder_74138_3_p9
  // _3_to_8_decoder__74138 #(.Facing("east")) 3_to_8_decoder_74138_4: pin names not known; wires that end beside it: A1, A0, B0, not_5_out, not_5_out, 1'b0, 1'b0, 1'b0, 1'b0, n3_to_8_decoder_74138_4_p10, n3_to_8_decoder_74138_4_p11
  // _3_to_8_decoder__74138 #(.Facing("east")) 3_to_8_decoder_74138_5: pin names not known; wires that end beside it: A0, B1, B0, n3_to_8_decoder_74138_5_p4
  // _3_to_8_decoder__74138 #(.Facing("east")) 3_to_8_decoder_74138_6: pin names not known; wires that end beside it: A1, A0, B0, 1'b1, not_7_out, 1'b0, 1'b0, 1'b0, 1'b0, n3_to_8_decoder_74138_6_p10
  // _3_to_8_decoder__74138 #(.Facing("east")) 3_to_8_decoder_74138_7: pin names not known; wires that end beside it: A1, A0, B1, not_7_out, 1'b0, 1'b0, n3_to_8_decoder_74138_7_p7, n3_to_8_decoder_74138_7_p8, n3_to_8_decoder_74138_7_p9, n3_to_8_decoder_74138_7_p10
  // _3_to_8_decoder__74138 #(.Facing("east")) 3_to_8_decoder_74138_8: pin names not known; wires that end beside it: A1, B1, B0, not_7_out, 1'b0, 1'b0, n3_to_8_decoder_74138_8_p7
  // _3_to_8_decoder__74138 #(.Facing("east")) 3_to_8_decoder_74138_9: pin names not known; wires that end beside it: A1, A0, B1, and_2_out, 1'b0, 1'b0, n3_to_8_decoder_74138_9_p7
  // _3_to_8_decoder__74138 #(.Facing("east")) 3_to_8_decoder_74138_10: pin names not known; wires that end beside it: A0, B1, B0, and_2_out, 1'b0, 1'b0, n3_to_8_decoder_74138_10_p7, n3_to_8_decoder_74138_10_p8
  and and_13 (and_13_out, A1, B1);
  or or_1 (or_1_out, not_11_out, not_13_out);
  and and_14 (and_14_out, A0, B0);
  or or_2 (or_2_out, not_12_out, not_10_out);
  and and_15 (and_15_out, not_10_out, not_12_out);
  or or_3 (or_3_out, A0, B0);
  and and_16 (and_16_out, not_11_out, not_13_out);
  xor xor_3 (xor_3_out, A1, B1);
  xor xor_4 (xor_4_out, A0, B0);
  xor xor_5 (xor_5_out, A1, B1);
  and and_17 (and_17_out, A1, B1);
  or or_4 (or_4_out, and_4_out, and_6_out);
  and and_18 (and_18_out, and_7_out, B1);
  and and_19 (and_19_out, B1, not_15_out);
  not not_15 (not_15_out, A1);
  xor xor_6 (xor_6_out, and_10_out, and_11_out);
  and and_20 (and_20_out, and_10_out, and_11_out);
  and and_21 (and_21_out, and_13_out, or_1_out);
  and and_22 (and_22_out, and_14_out, or_2_out);
  and and_23 (and_23_out, and_15_out, or_3_out);
  xor xor_7 (xor_7_out, xor_5_out, and_3_out);
  and and_24 (and_24_out, xor_5_out, and_3_out);
  or or_5 (or_5_out, or_4_out, and_18_out);
  xor xor_8 (xor_8_out, A1, B1);
  xor xor_9 (xor_9_out, and_9_out, xor_6_out);
  xor xor_10 (xor_10_out, and_20_out, and_12_out);
  and and_25 (and_25_out, and_20_out, and_12_out);
  not not_16 (not_16_out, n3_to_8_decoder_74138_2_p4);
  not not_17 (not_17_out, n3_to_8_decoder_74138_2_p5);
  not not_18 (not_18_out, n3_to_8_decoder_74138_2_p6);
  not not_19 (not_19_out, n3_to_8_decoder_74138_3_p7);
  not not_20 (not_20_out, n3_to_8_decoder_74138_3_p8);
  not not_21 (not_21_out, n3_to_8_decoder_74138_3_p9);
  not not_22 (not_22_out, n3_to_8_decoder_74138_4_p10);
  not not_23 (not_23_out, n3_to_8_decoder_74138_4_p11);
  not not_24 (not_24_out, not_12_out);
  not not_25 (not_25_out, A1);
  not not_26 (not_26_out, n3_to_8_decoder_74138_7_p8);
  not not_27 (not_27_out, n3_to_8_decoder_74138_7_p9);
  not not_28 (not_28_out, n3_to_8_decoder_74138_7_p10);
  not not_29 (not_29_out, n3_to_8_decoder_74138_8_p7);
  not not_30 (not_30_out, n3_to_8_decoder_74138_10_p8);
  or or_6 (or_6_out, A1, B1);
  and and_26 (and_26_out, or_6_out, or_7_out);
  or or_7 (or_7_out, A0, B0);
  or or_8 (or_8_out, B1, A1);
  and and_27 (and_27_out, or_8_out, and_16_out);
  not not_31 (not_31_out, xor_4_out);
  not not_32 (not_32_out, xor_3_out);
  or or_9 (or_9_out, and_24_out, and_17_out);
  xor xor_11 (xor_11_out, xor_8_out, and_8_out);
  and and_28 (and_28_out, and_8_out, not_33_out);
  not not_33 (not_33_out, xor_8_out);
  xor xor_12 (xor_12_out, xor_10_out, xor_9_out);
  and and_29 (and_29_out, xor_12_out, not_34_out);
  not not_34 (not_34_out, and_25_out);
  or or_10 (or_10_out, not_20_out, not_22_out);
  and and_30 (and_30_out, not_12_out, A1);
  or or_11 (or_11_out, not_21_out, not_23_out);
  and and_31 (and_31_out, not_24_out, not_25_out);
  nor nor_1 (nor_1_out, not_12_out, A1);
  and and_32 (and_32_out, B0, not_27_out);
  and and_33 (and_33_out, B0, not_35_out);
  not not_35 (not_35_out, n3_to_8_decoder_74138_7_p7);
  nand nand_1 (nand_1_out, n3_to_8_decoder_74138_9_p7, n3_to_8_decoder_74138_10_p7);
  and and_34 (and_34_out, not_30_out, A1);
  and and_35 (and_35_out, and_13_out, and_14_out);
  // _3_to_8_decoder__74138 #(.Facing("east")) 3_to_8_decoder_74138_11: pin names not known; wires that end beside it: and_1_out, and_26_out, and_23_out, and_27_out, and_1_out, 1'b0, 1'b0, n3_to_8_decoder_74138_11_p8
  and and_36 (and_36_out, xor_3_out, xor_4_out);
  and and_37 (and_37_out, xor_3_out, not_31_out);
  and and_38 (and_38_out, not_32_out, xor_4_out);
  nor nor_2 (nor_2_out, xor_4_out, xor_3_out);
  // _3_to_8_decoder__74138 #(.Facing("east")) 3_to_8_decoder_74138_12: pin names not known; wires that end beside it: xor_7_out, xor_1_out, or_9_out, not_3_out, 1'b0, 1'b0, n3_to_8_decoder_74138_12_p7, n3_to_8_decoder_74138_12_p8, n3_to_8_decoder_74138_12_p9, n3_to_8_decoder_74138_12_p10, n3_to_8_decoder_74138_12_p11, n3_to_8_decoder_74138_12_p12, n3_to_8_decoder_74138_12_p13
  // _3_to_8_decoder__74138 #(.Facing("east")) 3_to_8_decoder_74138_13: pin names not known; wires that end beside it: xor_11_out, xor_2_out, n3_to_8_decoder_74138_13_p3, not_8_out, 1'b0, 1'b0, n3_to_8_decoder_74138_13_p7, n3_to_8_decoder_74138_13_p8, n3_to_8_decoder_74138_13_p9, n3_to_8_decoder_74138_13_p10, n3_to_8_decoder_74138_13_p11, n3_to_8_decoder_74138_13_p12, n3_to_8_decoder_74138_13_p13
  or or_12 (n3_to_8_decoder_74138_13_p3, and_28_out, and_19_out);
  // _3_to_8_decoder__74138 #(.Facing("east")) 3_to_8_decoder_74138_14: pin names not known; wires that end beside it: and_9_out, xor_6_out, xor_10_out, not_4_out, 1'b0, 1'b0, n3_to_8_decoder_74138_14_p7, n3_to_8_decoder_74138_14_p8, n3_to_8_decoder_74138_14_p9, n3_to_8_decoder_74138_14_p10, n3_to_8_decoder_74138_14_p11, n3_to_8_decoder_74138_14_p12
  or or_13 (or_13_out, or_10_out, and_30_out);
  or or_14 (or_14_out, or_11_out, and_31_out);
  nand nand_2 (nand_2_out, n3_to_8_decoder_74138_5_p4, n3_to_8_decoder_74138_6_p10);
  or or_15 (or_15_out, nand_2_out, nor_1_out);
  and and_39 (and_39_out, B0, not_26_out);
  or or_16 (or_16_out, not_28_out, not_29_out);
  nor nor_3 (nor_3_out, and_21_out, or_17_out);
  or or_17 (or_17_out, and_22_out, and_35_out);
  or or_18 (or_18_out, and_23_out, and_27_out);
  not not_36 (not_36_out, n3_to_8_decoder_74138_12_p7);
  not not_37 (not_37_out, n3_to_8_decoder_74138_12_p8);
  not not_38 (not_38_out, n3_to_8_decoder_74138_12_p9);
  not not_39 (not_39_out, n3_to_8_decoder_74138_12_p10);
  not not_40 (not_40_out, n3_to_8_decoder_74138_12_p11);
  not not_41 (not_41_out, n3_to_8_decoder_74138_12_p12);
  not not_42 (not_42_out, n3_to_8_decoder_74138_12_p13);
  not not_43 (not_43_out, and_25_out);
  not not_44 (not_44_out, not_5_out);
  or or_19 (or_19_out, and_39_out, or_16_out);
  nor nor_4 (nor_4_out, nand_1_out, and_34_out);
  or or_20 (or_20_out, and_22_out, and_21_out);
  not not_45 (not_45_out, n3_to_8_decoder_74138_11_p8);
  or or_21 (or_21_out, and_37_out, and_38_out);
  assign L9 = not_3_out ? 1'b0 : 1'bz;  // Controlled_Buffer controlled_buffer_1
  assign L8 = not_3_out ? 1'b0 : 1'bz;  // Controlled_Buffer controlled_buffer_2
  assign L7 = not_3_out ? 1'b0 : 1'bz;  // Controlled_Buffer controlled_buffer_3
  not not_46 (not_46_out, n3_to_8_decoder_74138_13_p7);
  not not_47 (not_47_out, n3_to_8_decoder_74138_13_p8);
  not not_48 (not_48_out, n3_to_8_decoder_74138_13_p9);
  not not_49 (not_49_out, n3_to_8_decoder_74138_13_p10);
  not not_50 (not_50_out, n3_to_8_decoder_74138_13_p11);
  not not_51 (not_51_out, n3_to_8_decoder_74138_13_p12);
  not not_52 (not_52_out, n3_to_8_decoder_74138_13_p13);
  not not_53 (not_53_out, n3_to_8_decoder_74138_13_p3);
  not not_54 (not_54_out, not_8_out);
  not not_55 (not_55_out, n3_to_8_decoder_74138_14_p7);
  not not_56 (not_56_out, n3_to_8_decoder_74138_14_p8);
  not not_57 (not_57_out, n3_to_8_decoder_74138_14_p9);
  not not_58 (not_58_out, n3_to_8_decoder_74138_14_p10);
  not not_59 (not_59_out, n3_to_8_decoder_74138_14_p11);
  not not_60 (not_60_out, n3_to_8_decoder_74138_14_p12);
  assign L = not_5_out ? or_14_out : 1'bz;  // Controlled_Buffer controlled_buffer_4
  or or_22 (or_22_out, or_19_out, and_33_out);
  or or_23 (or_23_out, nand_1_out, and_34_out);
  assign L3 = and_1_out ? and_26_out : 1'bz;  // Controlled_Buffer controlled_buffer_5
  assign P = and_1_out ? or_18_out : 1'bz;  // Controlled_Buffer controlled_buffer_6
  assign L3 = not_2_out ? and_36_out : 1'bz;  // Controlled_Buffer controlled_buffer_7
  assign P = not_2_out ? or_21_out : 1'bz;  // Controlled_Buffer controlled_buffer_8
  assign L2 = not_2_out ? and_37_out : 1'bz;  // Controlled_Buffer controlled_buffer_9
  assign L1 = not_2_out ? and_38_out : 1'bz;  // Controlled_Buffer controlled_buffer_10
  assign L0 = not_2_out ? nor_2_out : 1'bz;  // Controlled_Buffer controlled_buffer_11
  or or_24 (or_24_out, not_48_out, not_52_out);
  and and_40 (and_40_out, not_56_out, not_43_out);
  assign L = not_44_out ? 1'b0 : 1'bz;  // Controlled_Buffer controlled_buffer_12
  assign G = not_44_out ? 1'b0 : 1'bz;  // Controlled_Buffer controlled_buffer_13
  assign E = not_44_out ? 1'b0 : 1'bz;  // Controlled_Buffer controlled_buffer_14
  assign L3 = not_7_out ? and_32_out : 1'bz;  // Controlled_Buffer controlled_buffer_15
  assign L2 = not_7_out ? and_33_out : 1'bz;  // Controlled_Buffer controlled_buffer_16
  assign L8 = and_2_out ? 1'b0 : 1'bz;  // Controlled_Buffer controlled_buffer_17
  assign L9 = and_2_out ? 1'b0 : 1'bz;  // Controlled_Buffer controlled_buffer_18
  assign L7 = and_2_out ? 1'b0 : 1'bz;  // Controlled_Buffer controlled_buffer_19
  assign L6 = and_2_out ? 1'b0 : 1'bz;  // Controlled_Buffer controlled_buffer_20
  assign L5 = and_2_out ? 1'b0 : 1'bz;  // Controlled_Buffer controlled_buffer_21
  assign L4 = and_2_out ? 1'b0 : 1'bz;  // Controlled_Buffer controlled_buffer_22
  assign L3 = and_2_out ? 1'b0 : 1'bz;  // Controlled_Buffer controlled_buffer_23
  assign L1 = not_6_out ? and_22_out : 1'bz;  // Controlled_Buffer controlled_buffer_24
  assign L0 = not_6_out ? nor_3_out : 1'bz;  // Controlled_Buffer controlled_buffer_25
  assign P = not_6_out ? or_20_out : 1'bz;  // Controlled_Buffer controlled_buffer_26
  assign L1 = and_1_out ? and_23_out : 1'bz;  // Controlled_Buffer controlled_buffer_27
  assign L2 = and_1_out ? and_27_out : 1'bz;  // Controlled_Buffer controlled_buffer_28
  assign L0 = and_1_out ? not_45_out : 1'bz;  // Controlled_Buffer controlled_buffer_29
  assign C = not_61_out ? 1'b0 : 1'bz;  // Controlled_Buffer controlled_buffer_30
  not not_61 (not_61_out, not_3_out);
  not not_62 (not_62_out, B0);
  and and_41 (and_41_out, not_62_out, not_16_out);
  and and_42 (and_42_out, B0, not_17_out);
  and and_43 (and_43_out, not_18_out, not_62_out);
  and and_44 (and_44_out, B0, not_19_out);
  assign L0 = not_7_out ? or_15_out : 1'bz;  // Controlled_Buffer controlled_buffer_31
  assign L1 = not_7_out ? or_19_out : 1'bz;  // Controlled_Buffer controlled_buffer_32
  assign P = not_7_out ? or_22_out : 1'bz;  // Controlled_Buffer controlled_buffer_33
  assign L2 = not_6_out ? and_21_out : 1'bz;  // Controlled_Buffer controlled_buffer_34
  assign L3 = not_6_out ? and_35_out : 1'bz;  // Controlled_Buffer controlled_buffer_35
  or or_25 (or_25_out, not_38_out, not_37_out);
  assign S = not_8_out ? or_5_out : 1'bz;  // Controlled_Buffer controlled_buffer_36
  or or_26 (or_26_out, not_47_out, not_50_out);
  or or_27 (or_27_out, or_24_out, and_45_out);
  and and_45 (and_45_out, not_47_out, not_53_out);
  assign P = not_4_out ? and_29_out : 1'bz;  // Controlled_Buffer controlled_buffer_37
  assign L0 = not_4_out ? not_55_out : 1'bz;  // Controlled_Buffer controlled_buffer_38
  or or_28 (or_28_out, and_41_out, and_42_out);
  or or_29 (or_29_out, and_43_out, and_44_out);
  assign L0 = and_2_out ? nor_4_out : 1'bz;  // Controlled_Buffer controlled_buffer_39
  assign L1 = and_2_out ? nand_1_out : 1'bz;  // Controlled_Buffer controlled_buffer_40
  assign P = and_2_out ? or_23_out : 1'bz;  // Controlled_Buffer controlled_buffer_41
  assign L2 = and_2_out ? and_34_out : 1'bz;  // Controlled_Buffer controlled_buffer_42
  assign L0 = not_3_out ? not_36_out : 1'bz;  // Controlled_Buffer controlled_buffer_43
  assign L2 = not_3_out ? not_37_out : 1'bz;  // Controlled_Buffer controlled_buffer_44
  assign L1 = not_3_out ? not_38_out : 1'bz;  // Controlled_Buffer controlled_buffer_45
  or or_30 (or_30_out, not_40_out, or_25_out);
  or or_31 (or_31_out, not_42_out, not_41_out);
  assign L0 = not_8_out ? not_46_out : 1'bz;  // Controlled_Buffer controlled_buffer_46
  assign L2 = not_8_out ? or_26_out : 1'bz;  // Controlled_Buffer controlled_buffer_47
  or or_32 (or_32_out, not_49_out, not_51_out);
  assign P = not_8_out ? or_27_out : 1'bz;  // Controlled_Buffer controlled_buffer_48
  assign L1 = not_4_out ? and_40_out : 1'bz;  // Controlled_Buffer controlled_buffer_49
  assign L2 = not_4_out ? not_57_out : 1'bz;  // Controlled_Buffer controlled_buffer_50
  assign L3 = not_4_out ? not_58_out : 1'bz;  // Controlled_Buffer controlled_buffer_51
  assign L4 = not_4_out ? not_59_out : 1'bz;  // Controlled_Buffer controlled_buffer_52
  assign E = not_5_out ? or_33_out : 1'bz;  // Controlled_Buffer controlled_buffer_53
  or or_33 (or_33_out, or_28_out, or_29_out);
  assign G = not_5_out ? or_13_out : 1'bz;  // Controlled_Buffer controlled_buffer_54
  assign L3 = not_3_out ? not_39_out : 1'bz;  // Controlled_Buffer controlled_buffer_55
  assign L4 = not_3_out ? not_40_out : 1'bz;  // Controlled_Buffer controlled_buffer_56
  assign L6 = not_3_out ? not_41_out : 1'bz;  // Controlled_Buffer controlled_buffer_57
  assign L5 = not_3_out ? not_42_out : 1'bz;  // Controlled_Buffer controlled_buffer_58
  or or_34 (or_34_out, or_31_out, not_40_out);
  assign L1 = not_8_out ? or_24_out : 1'bz;  // Controlled_Buffer controlled_buffer_59
  assign L3 = not_8_out ? or_32_out : 1'bz;  // Controlled_Buffer controlled_buffer_60
  assign S = not_54_out ? 1'b0 : 1'bz;  // Controlled_Buffer controlled_buffer_61
  assign L6 = not_4_out ? not_60_out : 1'bz;  // Controlled_Buffer controlled_buffer_62
  assign L9 = not_4_out ? and_25_out : 1'bz;  // Controlled_Buffer controlled_buffer_63
  assign L5 = not_4_out ? 1'b0 : 1'bz;  // Controlled_Buffer controlled_buffer_64
  assign L7 = not_4_out ? 1'b0 : 1'bz;  // Controlled_Buffer controlled_buffer_65
  assign L8 = not_4_out ? 1'b0 : 1'bz;  // Controlled_Buffer controlled_buffer_66
  assign L9 = not_7_out ? 1'b0 : 1'bz;  // Controlled_Buffer controlled_buffer_67
  assign L4 = not_7_out ? 1'b0 : 1'bz;  // Controlled_Buffer controlled_buffer_68
  assign L5 = not_7_out ? 1'b0 : 1'bz;  // Controlled_Buffer controlled_buffer_69
  assign L6 = not_7_out ? 1'b0 : 1'bz;  // Controlled_Buffer controlled_buffer_70
  assign L7 = not_7_out ? 1'b0 : 1'bz;  // Controlled_Buffer controlled_buffer_71
  assign L8 = not_7_out ? 1'b0 : 1'bz;  // Controlled_Buffer controlled_buffer_72
  assign L8 = not_7_out ? 1'b0 : 1'bz;  // Controlled_Buffer controlled_buffer_73
  assign P = not_3_out ? or_30_out : 1'bz;  // Controlled_Buffer controlled_buffer_74
  assign C = not_3_out ? or_34_out : 1'bz;  // Controlled_Buffer controlled_buffer_75
  assign L9 = not_8_out ? 1'b0 : 1'bz;  // Controlled_Buffer controlled_buffer_76
  assign L8 = not_8_out ? 1'b0 : 1'bz;  // Controlled_Buffer controlled_buffer_77
  assign L7 = not_8_out ? 1'b0 : 1'bz;  // Controlled_Buffer controlled_buffer_78
  assign L6 = not_8_out ? 1'b0 : 1'bz;  // Controlled_Buffer controlled_buffer_79
  assign L5 = not_8_out ? 1'b0 : 1'bz;  // Controlled_Buffer controlled_buffer_80
  assign L4 = not_8_out ? 1'b0 : 1'bz;  // Controlled_Buffer controlled_buffer_81
  assign L9 = not_5_out ? 1'b0 : 1'bz;  // Controlled_Buffer controlled_buffer_82
  assign L8 = not_5_out ? 1'b0 : 1'bz;  // Controlled_Buffer controlled_buffer_83
  assign L7 = not_5_out ? 1'b0 : 1'bz;  // Controlled_Buffer controlled_buffer_84
  assign L6 = not_5_out ? 1'b0 : 1'bz;  // Controlled_Buffer controlled_buffer_85
  assign L5 = not_5_out ? 1'b0 : 1'bz;  // Controlled_Buffer controlled_buffer_86
  assign L4 = not_5_out ? 1'b0 : 1'bz;  // Controlled_Buffer controlled_buffer_87
  assign P = not_5_out ? 1'b0 : 1'bz;  // Controlled_Buffer controlled_buffer_88
  assign L3 = not_5_out ? 1'b0 : 1'bz;  // Controlled_Buffer controlled_buffer_89
  assign L2 = not_5_out ? 1'b0 : 1'bz;  // Controlled_Buffer controlled_buffer_90
  assign L1 = not_5_out ? 1'b0 : 1'bz;  // Controlled_Buffer controlled_buffer_91
  assign L0 = not_5_out ? 1'b0 : 1'bz;  // Controlled_Buffer controlled_buffer_92
  assign L9 = not_6_out ? 1'b0 : 1'bz;  // Controlled_Buffer controlled_buffer_93
  assign L8 = not_6_out ? 1'b0 : 1'bz;  // Controlled_Buffer controlled_buffer_94
  assign L7 = not_6_out ? 1'b0 : 1'bz;  // Controlled_Buffer controlled_buffer_95
  assign L6 = not_6_out ? 1'b0 : 1'bz;  // Controlled_Buffer controlled_buffer_96
  assign L5 = not_6_out ? 1'b0 : 1'bz;  // Controlled_Buffer controlled_buffer_97
  assign L4 = not_6_out ? 1'b0 : 1'bz;  // Controlled_Buffer controlled_buffer_98
  assign L9 = and_1_out ? 1'b0 : 1'bz;  // Controlled_Buffer controlled_buffer_99
  assign L8 = and_1_out ? 1'b0 : 1'bz;  // Controlled_Buffer controlled_buffer_100
  assign L7 = and_1_out ? 1'b0 : 1'bz;  // Controlled_Buffer controlled_buffer_101
  assign L6 = and_1_out ? 1'b0 : 1'bz;  // Controlled_Buffer controlled_buffer_102
  assign L5 = and_1_out ? 1'b0 : 1'bz;  // Controlled_Buffer controlled_buffer_103
  assign L4 = and_1_out ? 1'b0 : 1'bz;  // Controlled_Buffer controlled_buffer_104
  assign L9 = not_2_out ? 1'b0 : 1'bz;  // Controlled_Buffer controlled_buffer_105
  assign L8 = not_2_out ? 1'b0 : 1'bz;  // Controlled_Buffer controlled_buffer_106
  assign L7 = not_2_out ? 1'b0 : 1'bz;  // Controlled_Buffer controlled_buffer_107
  assign L6 = not_2_out ? 1'b0 : 1'bz;  // Controlled_Buffer controlled_buffer_108
  assign L5 = not_2_out ? 1'b0 : 1'bz;  // Controlled_Buffer controlled_buffer_109
  assign L4 = not_2_out ? 1'b0 : 1'bz;  // Controlled_Buffer controlled_buffer_110

  assign L9_2 = L9;
  assign Z = L0;

  // Notes on the sheet:
  //   ADDER
  //   MULTI
  //   COMPARE
  //   DIVISION
  //   SUBTRACTER
  //   D0
  //   MOD
  //   BITWISE AND
  //   BITWISE OR
  //   BITWISE XOR
  //   D1
  //   10
  //   01
  //   01
  //   01
  //   00
  //   D2
  //   D3
  //   11
  //   10
  //   11-part
  //   01-part
  //   10-part
  //   11
  //   11
  //   10
  //   01
  //   00
  //   00-part
  //   10-part
  //   00
  //   Odd
  //   01-part
  //   00-part
  //   Odd
  //   Odd
  //   SET0
  //   SET0
  //   SET0
  //   SET0
endmodule
